# Fritzing sketch circuito (saved by Fritzing 0.9.4)
breadboards: 1

parts:
  R1 = Resistor [tolerance=±5% resistance=10k package=THT]
  R3 = Resistor [tolerance=±5% resistance=2k package=THT]
  R4 = Resistor [tolerance=±5% resistance=10k package=THT]
  R5 = Resistor [tolerance=±5% resistance=10k package=THT]
  R6 = Resistor [tolerance=±5% resistance=1k package=THT]
  J1 = Piezo Speaker
  LED1 = smd LED [color="Red (633nm)" package="0805 [SMD]"]
  LED2 = smd LED [color="Green (570nm)" package="0805 [SMD]"]
  LED3 = smd LED [color="Red (633nm)" package="0805 [SMD]"]
  LED4 = smd LED [color="Red (633nm)" package="0805 [SMD]"]
  Componente1 = Arduino Nano (Rev3.0) (ICSP)
  IR1 = TSOP312.., 314.. [package=THT]
  C1 = Electrolytic Capacitor [capacitance=220µF package="100 mil [THT, electrolytic]"]

nets:
  N1: R1.Pin_0, LED1.cathode
  GND: R1.Pin_1, R3.Pin_1, R4.Pin_1, J1.pin1, Componente1.GND, IR1.GND, C1.-
  N2: R3.Pin_0, LED2.cathode
  N3: R4.Pin_0, LED4.cathode
  N4: R5.Pin_0, LED3.cathode
  N5: R6.Pin_0, Componente1.D8
  N6: R6.Pin_1, J1.pin2
  N7: LED1.anode, Componente1.D2
  N8: LED2.anode, Componente1.D5
  N9: LED3.anode, Componente1.D4
  N10: LED4.anode, Componente1.D3
  N11: Componente1.D11/MOSI, IR1.Data
  N12: Componente1.5V, IR1.Vs, C1.+
